# Fritzing sketch G18C-Fritzing-Sketch (saved by Fritzing 0.9.3b)

parts:
  U1 = SPDT Slide Switch [package=ayz0202]
  M1 = DOIT Esp32 DevKit v1 (30 pins long, 11 pins width) [part_number=ESP32S-PIN30]
  U4 = Battery Holders [package=lipo-1100mAh]
  U5 = Battery Holders [package=lipo-1100mAh]
  M2 = RioRand LM2596
  Part1 = FC-03 [chip_label=FC-03]
  M3 = DC Motor
  WeMos_D1_Mini_Relay_Shield_V1 = WeMos D1 Mini Relay Shield V2

nets:
  N1: U1.2, U1.1, M1.D35
  3V3: U1.6, U1.5, M1.3V3, Part1.pin_1, WeMos_D1_Mini_Relay_Shield_V1.3V3
  N2: M1.GND, M2.Pin_4, Part1.pin_2, WeMos_D1_Mini_Relay_Shield_V1.G
  N3: M1.D34, Part1.pin_4
  N4: M1.D33, WeMos_D1_Mini_Relay_Shield_V1.D1
  N5: M1.VIN, M2.Pin_3
  N6: U4.+, U5.-
  N7: U4.-, M2.Pin_2, WeMos_D1_Mini_Relay_Shield_V1.COM
  N8: U5.+, M2.Pin_1, M3.pin_1
  N9: M3.pin_2, WeMos_D1_Mini_Relay_Shield_V1.NC

custom parts:
  DOIT Esp32 DevKit v1 (30 pins long, 11 pins width): The DOIT Esp32 DevKit v1 is one of the development board created by DOIT to evaluate the ESP-WROOM-32 module. It is based on the ESP32 microcontroller that boasts Wifi, Bluetooth, Ethernet and Low Power support all in a single chip. (vanepp) made breadboard work, adjusted pin numbering and labels and reduced size of schematic and cleaned up pcb. This chip is 30pins long (2 x15) and 11 pins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
  FC-03: FC-03, LM393 IR Speed Sensor Encoder
